# Fritzing sketch asus_to_hd120 (saved by Fritzing 0.9.3b)
breadboards: 1

parts:
  Composant1 = Arduino Nano (Rev3.0)
  R1 = Resistor [tolerance=±5% resistance=6.8k package=THT]
  R2 = Resistor [tolerance=±5% resistance=10k package=THT]
  R3 = Resistor [tolerance=±5% resistance=10k package=THT]
  R4 = Resistor [tolerance=±5% resistance=10k package=THT]
  R5 = Resistor [tolerance=±5% resistance=6.8k package=THT]
  R6 = Resistor [tolerance=±5% resistance=6.8k package=THT]
  J1 = female pin header, 4 pins [form="♀ (female)"]
  J2 = female pin header, 3 pins [form="♀ (female)"]

nets:
  N1: Composant1.GND, R1.Pin_0, R5.Pin_0, R6.Pin_0, J2.pin1
  N2: Composant1.D9, R4.Pin_0, R6.Pin_1
  N3: Composant1.D10, R3.Pin_0, R5.Pin_1
  N4: Composant1.D11/MOSI, R1.Pin_1, R2.Pin_0
  N5: Composant1.5V, J2.pin3
  N6: Composant1.A3, J2.pin2
  N7: R2.Pin_1, J1.pin2
  N8: R3.Pin_1, J1.pin3
  N9: R4.Pin_1, J1.pin4

notes:
  ASUS AURA CONNECTOR
  CORSAIR HUB
  GND
  5V
  DA
  12V
  G
  R
  B
